# Fritzing sketch Accelerometer Circuit (saved by Fritzing 0.9.3b)
breadboards: 1

parts:
  Part1 = Arduino Uno (Rev3) - ICSP
  VCC1 = Battery block 9V
  R1 = Resistor [tolerance=±5% resistance=220 package="2512 [SMD]"]
  R2 = Resistor [tolerance=±5% resistance=220 package="2512 [SMD]"]
  Q1 = Basic FET N-Channel [package="DPak [SMD]"]
  SP1 = SPEAKER [package=pcb_mount_speaker]
  Part2 = Triple Axis Accelerometer Breakout - ADXL335
  LED1 = RGB LED (com. cathode, rbg) [package="5 mm [THT]"]

nets:
  N1: Part1.A0, Part2.XOUT
  N2: Part1.A1, Part2.YOUT
  N3: Part1.A2, Part2.ZOUT
  N4: Part1.D9_PWM, LED1.green_anode
  N5: Part1.D11_PWM/MOSI, R2.Pin_1, Q1.source
  N6: Part1.D5_PWM, LED1.red_anode
  N7: Part1.D6_PWM, LED1.blue_anode
  3V3: Part1.3V3, Part2.VCC
  GND: Part1.GND, VCC1.-, R1.Pin_0, R2.Pin_0, Q1.Gate, Part2.GND
  N8: VCC1.+, SP1.-
  N9: R1.Pin_1, LED1.common_cathode
  N10: Q1.drain, SP1.+
